# Fritzing sketch fritzing_schematic (saved by Fritzing 1.0.4)

parts:
  M1 = ESP32-S3-DevKitC-1-N8R8-v1 [part_number=ESP32-S3-DevKitC-1-N8R8-v1]
  M2 = ps2 gamepad [package=THT]
  LCD1 = 2.8" SPI TFT Module [part_number=MSP2807]

nets:
  N1: M1.pin_1, M1.pin_2, M2.3.3V, LCD1.pin1, LCD1.pin8
  N2: M1.pin_8, LCD1.pin3
  N3: M1.pin_11, LCD1.pin7
  N4: M1.pin_23, M1.pin_44, M2.GND, LCD1.pin2
  N5: M1.pin_27, LCD1.pin6
  N6: M1.pin_34, M2.CLK
  N7: M1.pin_35, M2.ATT
  N8: M1.pin_36, M2.CMD
  N9: M1.pin_37, M2.DAT
  N10: M1.pin_40, LCD1.pin4

custom parts:
  ESP32-S3-DevKitC-1-N8R8-v1: ESP32-S3-DevKitC-1-N8R8-v1 This module is 44pins long (2x22) and 11 pins width.
  ps2 gamepad: PS2 gamepad. Warning! PCB view is designed for the female connector available from https://www.robotshop.com/en/ps2-connector.html. However there is no mechanical information that I can find so ipcb was generated from a scaled jpg and may well be wrong. Print the footprint out and check it against a real part before ordering boards!
  2.8" SPI TFT Module: A generic 2.8 inch LCD TFT 320x240 display with touchscreen and SD card slot. Uses the ILI9341 controller, like the Adafruit displays of this size uses.
